// Logisim project arq2_ex01.circ as structural Verilog: 5 circuits, main circuit 1/2 somador
module _1_2_somador (
  input  A0,
  input  B0,
  output SOMA,
  output CARRY_OUT
);

  xor xor_1 (SOMA, A0, B0);
  and and_1 (CARRY_OUT, A0, B0);
endmodule

module _1_bit_somador (
  input  in_1,
  input  in_2,
  input  in_3,
  output out_4,
  output out_5
);

  wire n1_2_somador_1_carry_out, n1_2_somador_1_soma, n1_2_somador_2_carry_out;

  _1_2_somador u_1_2_somador_1 (.A0(in_2), .B0(in_3), .SOMA(n1_2_somador_1_soma), .CARRY_OUT(n1_2_somador_1_carry_out));
  _1_2_somador u_1_2_somador_2 (
    .A0(n1_2_somador_1_soma), .B0(in_1), .SOMA(out_4), .CARRY_OUT(n1_2_somador_2_carry_out));
  or or_1 (out_5, n1_2_somador_2_carry_out, n1_2_somador_1_carry_out);
endmodule

module _4_bit_somador (
  input  Ci0,
  input  A0,
  input  B0,
  input  A1,
  input  B1,
  input  A2,
  input  B2,
  input  A3,
  input  B3,
  output S0,
  output S1,
  output S2,
  output S3,
  output flag_0,
  output flag_negativo,
  output Overflow,
  output Co0
);

  wire n1_bit_somador_1_out_5, n1_bit_somador_2_out_5, n1_bit_somador_3_out_5;

  _1_bit_somador u_1_bit_somador_1 (.in_1(Ci0), .in_2(A0), .in_3(B0), .out_4(S0), .out_5(n1_bit_somador_1_out_5));
  _1_bit_somador u_1_bit_somador_2 (
    .in_1(n1_bit_somador_1_out_5), .in_2(A1), .in_3(B1), .out_4(S1), .out_5(n1_bit_somador_2_out_5));
  _1_bit_somador u_1_bit_somador_3 (
    .in_1(n1_bit_somador_2_out_5), .in_2(A2), .in_3(B2), .out_4(S2), .out_5(n1_bit_somador_3_out_5));
  _1_bit_somador u_1_bit_somador_4 (
    .in_1(n1_bit_somador_3_out_5), .in_2(A3), .in_3(B3), .out_4(flag_negativo), .out_5(Co0));
  xor xor_1 (Overflow, n1_bit_somador_3_out_5, Co0);
  nor nor_1 (flag_0, S0, S1, S2, flag_negativo);

  assign S3 = flag_negativo;
endmodule

module main (
  input  A3,
  input  A2,
  input  Ci,
  input  A1,
  input  A0,
  input  B3,
  input  B2,
  input  B1,
  input  B0,
  output S0,
  output S1,
  output S2,
  output S3,
  output Flag_0,
  output Flag_Negativo,
  output Co,
  output Overflow
);

  wire decodificador_1_a, decodificador_1_b, decodificador_1_c, decodificador_1_d, decodificador_1_dp,
       decodificador_1_e, decodificador_1_f, decodificador_1_g, decodificador_2_a, decodificador_2_b,
       decodificador_2_c, decodificador_2_d, decodificador_2_dp, decodificador_2_e, decodificador_2_f,
       decodificador_2_g, decodificador_3_a, decodificador_3_b, decodificador_3_c, decodificador_3_d,
       decodificador_3_dp, decodificador_3_e, decodificador_3_f, decodificador_3_g;

  Decodificador decodificador_1 (
    .E3(A3), .E2(A2), .E1(A1), .E0(A0), .a(decodificador_1_a), .b(decodificador_1_b), .c(decodificador_1_c),
    .d(decodificador_1_d), .e(decodificador_1_e), .f(decodificador_1_f), .g(decodificador_1_g),
    .dp(decodificador_1_dp));
  _7_Segment_Display u_7_segment_display_1 (
    .g(decodificador_1_g), .f(decodificador_1_f), .a(decodificador_1_a), .b(decodificador_1_b),
    .e(decodificador_1_e), .d(decodificador_1_d), .c(decodificador_1_c), .dp(decodificador_1_dp));
  _4_bit_somador u_4_bit_somador_1 (
    .A0(A0), .B0(B0), .A1(A1), .B1(B1), .A2(A2), .B2(B2), .A3(A3), .B3(B3), .Ci0(Ci), .Co0(Co), .S0(S0),
    .S1(S1), .S2(S2), .S3(S3), .flag_0(Flag_0), .flag_negativo(Flag_Negativo), .Overflow(Overflow));
  Decodificador decodificador_2 (
    .E3(B3), .E2(B2), .E1(B1), .E0(B0), .a(decodificador_2_a), .b(decodificador_2_b), .c(decodificador_2_c),
    .d(decodificador_2_d), .e(decodificador_2_e), .f(decodificador_2_f), .g(decodificador_2_g),
    .dp(decodificador_2_dp));
  _7_Segment_Display u_7_segment_display_2 (
    .g(decodificador_2_g), .f(decodificador_2_f), .a(decodificador_2_a), .b(decodificador_2_b),
    .e(decodificador_2_e), .d(decodificador_2_d), .c(decodificador_2_c), .dp(decodificador_2_dp));
  Decodificador decodificador_3 (
    .E3(S3), .E2(S2), .E1(S1), .E0(S0), .a(decodificador_3_a), .b(decodificador_3_b), .c(decodificador_3_c),
    .d(decodificador_3_d), .e(decodificador_3_e), .f(decodificador_3_f), .g(decodificador_3_g),
    .dp(decodificador_3_dp));
  _7_Segment_Display u_7_segment_display_3 (
    .g(decodificador_3_g), .f(decodificador_3_f), .a(decodificador_3_a), .b(decodificador_3_b),
    .e(decodificador_3_e), .d(decodificador_3_d), .c(decodificador_3_c), .dp(decodificador_3_dp));
endmodule

module Decodificador (
  input  E3,
  input  E2,
  input  E1,
  input  E0,
  output a,
  output b,
  output c,
  output d,
  output e,
  output f,
  output g,
  output dp
);

  wire and_1_out, and_2_out, and_3_out, and_4_out, and_5_out, and_6_out, and_7_out, and_8_out, and_9_out,
       and_10_out, and_11_out, and_12_out, and_13_out, and_14_out, and_15_out, and_16_out, and_17_out,
       and_18_out, and_19_out, and_20_out, and_21_out, and_22_out, and_23_out, and_24_out, and_25_out,
       and_26_out, and_27_out, and_28_out, and_29_out, and_30_out, and_31_out, and_32_out, and_33_out,
       and_34_out, and_35_out, not_1_out, not_2_out, not_3_out, not_4_out, not_5_out, not_6_out, not_7_out,
       not_8_out, not_9_out, not_10_out, not_11_out, not_12_out, not_13_out, not_14_out, not_15_out,
       not_16_out, not_17_out, not_18_out, not_19_out, not_20_out, not_21_out, not_22_out, not_23_out,
       not_24_out, not_25_out, not_26_out, not_27_out, not_28_out, not_29_out, not_30_out, not_31_out,
       not_32_out, not_33_out, not_34_out, not_35_out, not_36_out, not_37_out, not_38_out, not_39_out,
       not_40_out, not_41_out, not_42_out, not_43_out;

  not not_1 (not_1_out, E2);
  and and_1 (and_1_out, not_1_out, not_2_out);
  not not_2 (not_2_out, E0);
  not not_3 (not_3_out, E3);
  and and_2 (and_2_out, not_3_out, E1);
  not not_4 (not_4_out, E3);
  and and_3 (and_3_out, not_4_out, E2, E0);
  and and_4 (and_4_out, E2, E1);
  and and_5 (and_5_out, E3, not_5_out, not_6_out);
  not not_5 (not_5_out, E2);
  not not_6 (not_6_out, E1);
  and and_6 (and_6_out, E3, not_7_out);
  not not_7 (not_7_out, E0);
  not not_8 (not_8_out, E3);
  and and_7 (and_7_out, not_8_out, not_9_out);
  not not_9 (not_9_out, E2);
  not not_10 (not_10_out, E3);
  not not_11 (not_11_out, E1);
  and and_8 (and_8_out, not_10_out, not_11_out, not_12_out);
  not not_12 (not_12_out, E0);
  not not_13 (not_13_out, E2);
  and and_9 (and_9_out, not_13_out, not_14_out);
  not not_14 (not_14_out, E0);
  not not_15 (not_15_out, E3);
  and and_10 (and_10_out, not_15_out, E1, E0);
  not not_16 (not_16_out, E1);
  and and_11 (and_11_out, E3, not_16_out, E0);
  not not_17 (not_17_out, E3);
  and and_12 (and_12_out, not_17_out, not_18_out);
  not not_18 (not_18_out, E1);
  not not_19 (not_19_out, E3);
  and and_13 (and_13_out, not_19_out, E0);
  not not_20 (not_20_out, E1);
  and and_14 (and_14_out, not_20_out, E0);
  not not_21 (not_21_out, E3);
  and and_15 (and_15_out, not_21_out, E2);
  and and_16 (and_16_out, E3, not_22_out);
  not not_22 (not_22_out, E2);
  not not_23 (not_23_out, E3);
  and and_17 (and_17_out, not_23_out, not_24_out, not_25_out);
  not not_24 (not_24_out, E2);
  not not_25 (not_25_out, E0);
  not not_26 (not_26_out, E2);
  and and_18 (and_18_out, not_26_out, E1, E0);
  and and_19 (and_19_out, E2, not_27_out, E0);
  not not_27 (not_27_out, E1);
  and and_20 (and_20_out, E2, E1, not_28_out);
  not not_28 (not_28_out, E0);
  and and_21 (and_21_out, E3, not_29_out);
  not not_29 (not_29_out, E1);
  not not_30 (not_30_out, E2);
  and and_22 (and_22_out, not_30_out, not_31_out);
  not not_31 (not_31_out, E0);
  and and_23 (and_23_out, E1, not_32_out);
  not not_32 (not_32_out, E0);
  and and_24 (and_24_out, E3, E1);
  and and_25 (and_25_out, E3, E2);
  not not_33 (not_33_out, E1);
  and and_26 (and_26_out, not_33_out, not_34_out);
  not not_34 (not_34_out, E0);
  not not_35 (not_35_out, E3);
  and and_27 (and_27_out, not_35_out, E2, not_36_out);
  not not_36 (not_36_out, E1);
  and and_28 (and_28_out, E2, not_37_out);
  not not_37 (not_37_out, E0);
  and and_29 (and_29_out, E3, not_38_out);
  not not_38 (not_38_out, E2);
  and and_30 (and_30_out, E3, E1);
  not not_39 (not_39_out, E2);
  and and_31 (and_31_out, not_39_out, E1);
  and and_32 (and_32_out, E1, not_40_out);
  not not_40 (not_40_out, E0);
  not not_41 (not_41_out, E3);
  and and_33 (and_33_out, not_41_out, E2, not_42_out);
  not not_42 (not_42_out, E1);
  and and_34 (and_34_out, E3, not_43_out);
  not not_43 (not_43_out, E2);
  and and_35 (and_35_out, E3, E0);
  or or_1 (b, and_7_out, and_8_out, and_9_out, and_10_out, and_11_out);
  or or_2 (c, and_12_out, and_13_out, and_14_out, and_15_out, and_16_out);
  or or_3 (d, and_17_out, and_18_out, and_19_out, and_20_out, and_21_out);
  or or_4 (e, and_22_out, and_23_out, and_24_out, and_25_out);
  or or_5 (f, and_26_out, and_27_out, and_28_out, and_29_out, and_30_out);
  or or_6 (g, and_31_out, and_32_out, and_33_out, and_34_out, and_35_out);
  or or_7 (a, and_1_out, and_2_out, and_3_out, and_4_out, and_5_out, and_6_out);

  assign dp = 1'b0;
endmodule
