// Logisim project arq2_ep2_pt2.circ as structural Verilog: 5 circuits, main circuit main
module main (
  input  binvert,
  input  cin,
  input  a0,
  input  b0,
  input  a1,
  input  b1,
  input  a2,
  input  b2,
  input  a3,
  input  b3,
  input  OP1,
  input  OP0,
  output S0,
  output S1,
  output S2,
  output S3,
  output CO
);

  wire ula_1bit_1_co, ula_1bit_2_co, ula_1bit_3_co;

  ULA_1bit ula_1bit_1 (.a(a0), .b(b0), .binvert(binvert), .cin(cin), .OP1(OP1), .OP0(OP0), .co(ula_1bit_1_co), .s(S0));
  ULA_1bit ula_1bit_2 (
    .a(a1), .b(b1), .binvert(binvert), .cin(ula_1bit_1_co), .OP1(OP1), .OP0(OP0), .co(ula_1bit_2_co), .s(S1));
  ULA_1bit ula_1bit_3 (
    .a(a2), .b(b2), .binvert(binvert), .cin(ula_1bit_2_co), .OP1(OP1), .OP0(OP0), .co(ula_1bit_3_co), .s(S2));
  ULA_1bit ula_1bit_4 (.a(a3), .b(b3), .binvert(binvert), .cin(ula_1bit_3_co), .OP1(OP1), .OP0(OP0), .co(CO), .s(S3));
endmodule

module ULA_1bit (
  input  binvert,
  input  cin,
  input  a,
  input  b,
  input  OP1,
  input  OP0,
  output s,
  output co
);

  wire and_1_out, mux_2x1_1_s, not_1_out, not_2_out, or_1_out, somador_1bit_1_soma;

  not not_1 (not_1_out, b);
  mux_2X1 mux_2x1_1 (.in0(b), .in1(not_1_out), .S(mux_2x1_1_s), .binvert(binvert));
  and and_1 (and_1_out, a, b);
  or or_1 (or_1_out, a, b);
  not not_2 (not_2_out, a);
  somador_1bit somador_1bit_1 (.a(a), .b(mux_2x1_1_s), .in_1(cin), .co(co), .soma(somador_1bit_1_soma));
  MUX mux_1 (.M(and_1_out), .N(or_1_out), .O(not_2_out), .P(somador_1bit_1_soma), .OP1(OP1), .OP0(OP0), .S(s));
endmodule

module MUX (
  input  M,
  input  N,
  input  O,
  input  P,
  input  OP1,
  input  OP0,
  output S
);

  wire and_1_out, and_2_out, and_3_out, and_4_out, not_1_out, not_2_out, not_3_out, not_4_out;

  and and_1 (and_1_out, M, not_1_out, not_2_out);
  not not_1 (not_1_out, OP1);
  not not_2 (not_2_out, OP0);
  not not_3 (not_3_out, OP1);
  and and_2 (and_2_out, N, not_3_out, OP0);
  and and_3 (and_3_out, O, OP1, not_4_out);
  not not_4 (not_4_out, OP0);
  and and_4 (and_4_out, P, OP1, OP0);
  or or_1 (S, and_1_out, and_2_out, and_3_out, and_4_out);
endmodule

module somador_1bit (
  input  in_1,
  input  a,
  input  b,
  output soma,
  output co
);

  wire and_1_out, and_2_out, xor_1_out;

  xor xor_1 (xor_1_out, a, b);
  and and_1 (and_1_out, a, b);
  xor xor_2 (soma, xor_1_out, in_1);
  and and_2 (and_2_out, xor_1_out, in_1);
  or or_1 (co, and_2_out, and_1_out);
endmodule

module mux_2X1 (
  input  in0,
  input  in1,
  input  binvert,
  output S
);

  wire and_1_out, and_2_out, not_1_out;

  and and_1 (and_1_out, binvert, in1);
  not not_1 (not_1_out, binvert);
  and and_2 (and_2_out, not_1_out, in0);
  or or_1 (S, and_1_out, and_2_out);
endmodule
